# Fritzing sketch lightsaberFritzing (saved by Fritzing 0.9.10b)
circuit board: 8.46667cm x 5.64444cm
breadboards: 1

parts:
  Teensy1 = Teensy 3.6 (Basic)
  LED1 = LED - 5mm [color="Red (633nm)" current=30mA package="5 mm [THT]"]
  Q2 = NPN-Transistor [package="TO92 [THT]"]
  TP1 = TP4056 [chip_label=TP4056 package="DIP (Dual Inline) [THT]"]
  U1 = LIPO-1000mAh [package=lipo-1000]
  Part1 = Adafruit MAX98357A I2S 3W Class D Amplifier [part_number="Adafruit #3006"]
  SP1 = SPEAKER [package=pcb_mount_speaker]
  R2 = Resistor [tolerance=±5% resistance=10k power=0.25 package=THT]
  LED2 = LED - 5mm [color="Red (633nm)" current=30mA package="5 mm [THT]"]
  S1 = Pushbutton [package="[THT]"]

nets:
  GND: Teensy1.GND, Q2.E, TP1.pin6, Part1.GND, S1.Pin_3, S1.Pin_4
  N1: Teensy1.D9, Part1.BCLK
  N2: Teensy1.A7/D21, Teensy1.A11
  N3: Teensy1.A8/D22, Teensy1.A10, Part1.DIN
  N4: Teensy1.A9/D23, Teensy1.AREF, Part1.LRCLK
  3V3: Teensy1.3V3, Teensy1.3V3_1, LED1.anode, Part1.VIN, LED2.anode
  N5: Teensy1.AGND, Teensy1.VUSB
  N6: Teensy1.Vin, TP1.pin3
  N7: Teensy1.D27, Teensy1.3V, Teensy1.Vb
  N8: Teensy1.D32, R2.Pin_1
  N9: Teensy1.D38, Teensy1.R
  N10: LED1.cathode, Q2.C, LED2.cathode
  N11: Q2.B, R2.Pin_0
  N12: TP1.pin4, U1.+
  N13: TP1.pin5, U1.-
  N14: Part1.VO-, SP1.+
  N15: Part1.VO+, SP1.-
  N16: S1.Pin_1, S1.Pin_2

custom parts:
  Teensy 3.6 (Basic): The Teensy is a complete USB-based microcontoller development system, in a very small footprint, capable of implementing many types of projects. All programming is done via the USB port. No special programmer is needed, only a standard micro-USB cable and a PC or Macintosh with a USB port.
  TP4056: A DIP stand-in part for whatever IC you want. With 6 pins on a 300mil dual inline package (DIP) footprint.
  Adafruit MAX98357A I2S 3W Class D Amplifier: Listen to this good news - we now have an all in one digital audio amp breakout board that works incredibly well with the Raspberry Pi! If you're looking for an easy and low cost way to get you digital sound files bumpin' then the MAX08357 I2S Amp Breakout is for you. It takes standard I2S digital audio input and, not only decodes it into analog, but also amplifies it directly into a speaker.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
